// Logisim project BeEight.circ as structural Verilog: 1 circuit, main circuit main
module main (
);

  wire [11:0] ProgramCounter_q;

  Counter #(.max('hfff), .width(12)) ProgramCounter (.Q(ProgramCounter_q));  // open: clr, load, up, count, clk, D, carry
  ROM #(.addrWidth(12)) rom_1 (.addr(ProgramCounter_q));  // open: data
  Register Accumulator ();  // open: D, en, clk, Q, clr
  Register PrimBuffer ();  // open: D, en, clk, Q, clr
  Register SecBuffer ();  // open: D, en, clk, Q, clr
  ROM rom_2 ();  // open: addr, data

  // Notes on the sheet:
  //   contents of rom_1 (hex, n*v repeats v):
  //   0 37 86 66 96 65 20 10 a6 65 30 18 b5 55
endmodule
